# Fritzing sketch energy_cost (saved by Fritzing 1.0.4)
breadboards: 1

parts:
  元件1 = Arduino MKR WiFi 1010
  DC_Mot_Enc1 = DC Motor with two-phase hall-encoder [part_number=VT-E-G25A-06-177E]
  元件3 = Adafruit TB6612 DC and Stepper Motor Driver [part_number="Adafruit #2448"]
  INA3 = INA219 DC Current Sensor Breakout
  A1 = Pololu DV24V50F5
  VCC1 = 4 x AAA Battery Mount [internal_resistance=0.1Ω]

nets:
  N1: 元件1.D2_PWM, 元件3.STBY
  N2: 元件1.D3_PWM, 元件3.AIN1
  N3: 元件1.D4_PWM, 元件3.AIN2
  N4: 元件1.D5_PWM, 元件3.PWMA
  N5: 元件1.D6, DC_Mot_Enc1.pin5
  N6: 元件1.D7, DC_Mot_Enc1.pin6
  N7: 元件1.D11_SDA, INA3.SDA
  N8: 元件1.D12_SCL, INA3.SCL
  GND: 元件1.GND, DC_Mot_Enc1.pin4, INA3.GND, A1.Pin_3, VCC1.-
  VCC: 元件1.VCC, DC_Mot_Enc1.pin3, 元件3.VCC, INA3.VCC
  N9: DC_Mot_Enc1.pin1, 元件3.MOTORA2
  N10: DC_Mot_Enc1.pin2, 元件3.MOTORA1
  N11: 元件3.PWRIN, INA3.Vin-
  N12: INA3.Vin+, A1.Pin_5
  N13: A1.Pin_2, VCC1.+

custom parts:
  Arduino MKR WiFi 1010: This is the newest version of the MKR 1000 WIFI, but with an ESP32 module on board made by U-BLOX.
  Adafruit TB6612 DC and Stepper Motor Driver: Spin two DC motors, step one bi-polar or uni-polar stepper, or fire off two solenoids with 1.2A per channel using the TB6612. These are perhaps better known as "the drivers in our assembled Adafruit Motorshield or Motor HAT." We really like these dual H-bridges, so if you want to control motors without a shield or HAT these are easy to include on any solderless breadboard or perma-proto.
  INA219 DC Current Sensor Breakout: INA DC Current Sensor Breakout
  Pololu DV24V50F5: This small synchronous switching step-down (or buck) regulator takes an input voltage of up to 38 V and efficiently reduces it to 5 V.
