# Fritzing sketch fixed_final (saved by Fritzing 1.0.4)
breadboards: 1

parts:
  元件1 = Arduino MKR WiFi 1010
  R1 = Photocell (LDR) [power=0.25W dark_resistance_@0.01lx=300kΩ light_resistance_@100lx=400Ω luminance=10lx package=THT]
  R2 = Photocell (LDR) [power=0.25W dark_resistance_@0.01lx=300kΩ light_resistance_@100lx=400Ω luminance=10lx package=THT]
  INA1 = INA219 DC Current Sensor Breakout
  INA2 = INA219 DC Current Sensor Breakout
  元件2 = Adafruit BQ24074 Solar-DC-USB Lipo Charger
  Part1 = Solar Panel [package="Renogy 50 Watts 12 Volt Monocrystalline Bendable Solar Panel"]
  U1 = LIPO-2000mAh [package=lipo-2000]
  A1 = Pololu DV24V50F5
  R3 = Resistor [tolerance=±5% resistance=10K package="2512 [SMD]"]
  R4 = Resistor [tolerance=±5% resistance=10K package="2512 [SMD]"]

nets:
  N1: 元件1.A1, R2.pin_0, R4.Pin_1
  N2: 元件1.A2, R1.pin_0, R3.Pin_1
  N3: 元件1.D11_SDA, INA1.SDA, INA2.SDA
  N4: 元件1.D12_SCL, INA1.SCL, INA2.SCL
  GND: 元件1.GND, R1.pin_1, R2.pin_1, INA1.GND, INA2.GND, 元件2.GND, Part1.Connector_2, U1.-, A1.Pin_3
  VCC: 元件1.VCC, INA1.VCC, INA2.VCC, R3.Pin_0, R4.Pin_0
  N5: 元件1.VIN, INA2.Vin-
  N6: INA1.Vin-, 元件2.VBUS
  N7: INA1.Vin+, Part1.Connector_1
  N8: INA2.Vin+, A1.Pin_5
  N9: 元件2.VLIPO, U1.+
  N10: 元件2.OUT, A1.Pin_2

custom parts:
  Arduino MKR WiFi 1010: This is the newest version of the MKR 1000 WIFI, but with an ESP32 module on board made by U-BLOX.
  INA219 DC Current Sensor Breakout: INA DC Current Sensor Breakout
  Solar Panel: Renogy 50 Watts 12 Volt Solar Panel
  Pololu DV24V50F5: This small synchronous switching step-down (or buck) regulator takes an input voltage of up to 38 V and efficiently reduces it to 5 V.
