# Fritzing sketch single_final (saved by Fritzing 1.0.4)
breadboards: 1

parts:
  元件1 = Arduino MKR WiFi 1010
  R1 = Photocell (LDR) [power=0.25W dark_resistance_@0.01lx=300kΩ light_resistance_@100lx=400Ω luminance=10lx package=THT]
  R2 = Photocell (LDR) [power=0.25W dark_resistance_@0.01lx=300kΩ light_resistance_@100lx=400Ω luminance=10lx package=THT]
  INA1 = INA219 DC Current Sensor Breakout
  INA2 = INA219 DC Current Sensor Breakout
  元件2 = Adafruit BQ24074 Solar-DC-USB Lipo Charger
  Part1 = Solar Panel [package="Renogy 50 Watts 12 Volt Monocrystalline Bendable Solar Panel"]
  U1 = LIPO-2000mAh [package=lipo-2000]
  R3 = Resistor [tolerance=±5% resistance=10K package="2512 [SMD]"]
  R4 = Resistor [tolerance=±5% resistance=10K package="2512 [SMD]"]
  DC_Mot_Enc1 = DC Motor with two-phase hall-encoder [part_number=VT-E-G25A-06-177E]
  元件3 = Adafruit TB6612 DC and Stepper Motor Driver [part_number="Adafruit #2448"]
  INA3 = INA219 DC Current Sensor Breakout
  A1 = Pololu DV24V50F5
  元件5 = Adafruit DS3231 [part_number="Adafruit #3013"]
  A2 = Pololu DV24V50F5

nets:
  N1: 元件1.A0_DAC0, R2.pin_0, R4.Pin_1
  N2: 元件1.A1, R1.pin_0, R3.Pin_1
  N3: 元件1.D2_PWM, 元件3.STBY
  N4: 元件1.D3_PWM, 元件3.AIN1
  N5: 元件1.D4_PWM, 元件3.AIN2
  N6: 元件1.D5_PWM, 元件3.PWMA
  N7: 元件1.D6, DC_Mot_Enc1.pin5
  N8: 元件1.D7, DC_Mot_Enc1.pin6
  N9: 元件1.D11_SDA, INA1.SDA, INA2.SDA, INA3.SDA, 元件5.SDA
  N10: 元件1.D12_SCL, INA1.SCL, INA2.SCL, INA3.SCL, 元件5.SCL
  GND: 元件1.GND, R1.pin_1, R2.pin_1, INA1.GND, INA2.GND, 元件2.GND, Part1.Connector_2, U1.-, DC_Mot_Enc1.pin4, 元件3.GND, INA3.GND, A1.Pin_3, 元件5.GND, A2.Pin_3, A2.Pin_4
  VCC: 元件1.VCC, INA1.VCC, INA2.VCC, R3.Pin_0, R4.Pin_0, DC_Mot_Enc1.pin3, 元件3.VCC, INA3.VCC, 元件5.Vin
  N11: 元件1.VIN, INA2.Vin-
  N12: INA1.Vin-, 元件2.VBUS
  N13: INA1.Vin+, Part1.Connector_1
  N14: INA2.Vin+, A2.Pin_5
  N15: 元件2.VLIPO, U1.+
  N16: 元件2.OUT, A1.Pin_2, A2.Pin_2
  N17: DC_Mot_Enc1.pin1, 元件3.MOTORA2
  N18: DC_Mot_Enc1.pin2, 元件3.MOTORA1
  N19: 元件3.PWRIN, INA3.Vin-
  N20: INA3.Vin+, A1.Pin_5

custom parts:
  Arduino MKR WiFi 1010: This is the newest version of the MKR 1000 WIFI, but with an ESP32 module on board made by U-BLOX.
  INA219 DC Current Sensor Breakout: INA DC Current Sensor Breakout
  Solar Panel: Renogy 50 Watts 12 Volt Solar Panel
  Adafruit TB6612 DC and Stepper Motor Driver: Spin two DC motors, step one bi-polar or uni-polar stepper, or fire off two solenoids with 1.2A per channel using the TB6612. These are perhaps better known as "the drivers in our assembled Adafruit Motorshield or Motor HAT." We really like these dual H-bridges, so if you want to control motors without a shield or HAT these are easy to include on any solderless breadboard or perma-proto.
  Pololu DV24V50F5: This small synchronous switching step-down (or buck) regulator takes an input voltage of up to 38 V and efficiently reduces it to 5 V.
  Adafruit DS3231: The datasheet for the DS3231 explains that this part is an "Extremely Accurate I²C-Integrated RTC/TCXO/Crystal". And, hey, it does exactly what it says on the tin! This Real Time Clock (RTC) is the most precise you can get in a small, low power package. Most RTCs use an external 32kHz timing crystal that is used to keep time with low current draw. And that's all well and good, but those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
